# Fritzing sketch Rangkaian alarm kebakaran (saved by Fritzing 0.9.3b)
breadboards: 1

parts:
  DHT1 = DHT22 Humidity and Temperature Sensor
  Mod1 = MQ-7 breakout
  buz1 = Piezo Buzzer
  LED2 = LED - 3mm [color="Red (633nm)" package="3 mm [THT]"]
  S1 = KY-026
  U1 = ESP8266 NodeMCU LoLin module
  R1 = Resistor [tolerance=±5% resistance=220 package="1206 [SMD]"]
  R2 = Resistor [tolerance=±5% resistance=220 package="1206 [SMD]"]

nets:
  VDD: DHT1.VDD, U1.3V3
  GND: DHT1.GND, U1.GND, R2.Pin_0
  N1: Mod1.AO, U1.A0
  N2: buz1.pin_1, U1.D2
  N3: LED2.cathode, R2.Pin_1
  N4: LED2.anode, U1.D0
  N5: S1.pin4, U1.D1
  N6: U1.D3, R1.Pin_1

notes:
  Flame --- Nodemcu
  D0 --- D1
  VCC --- 5V
  GND --- GND
  MQ2 -- Nodemcu
  VCC -- 3V
  GND -- GND
  A0 -- A0

custom parts:
  MQ-7 breakout: MQ-5 gas sensor
  Piezo Buzzer: Part from https://www.nutsvolts.com/magazine/article/november2012_SmileysWorkshop modified to be .3 in spacing to match the adafruit buzzer 5V breadboard friendly part.
  KY-026: ky-026 flame sensor module
  ESP8266 NodeMCU LoLin module: ESP8266 based NodeMCU
